# Fritzing sketch robohelp (saved by Fritzing 0.9.5d)
breadboards: 1

parts:
  Компонент1 = Arduino Nano (Rev3.0)
  HC-SR04_Sensor_1 = HC-SR04 Ultrasonic Distance Sensor
  R1 = Photocell (LDR) [package=THT]
  R2 = Resistor [tolerance=±5% resistance=10k package=THT]
  7_Segment1 = 7 Segment Display
  IC1 = SHIFT REGISTER [package=dil16]  # not connected

nets:
  GND: Компонент1.GND, HC-SR04_Sensor_1.GND, R2.Pin_1
  N1: Компонент1.D4, HC-SR04_Sensor_1.TRIG
  N2: Компонент1.D5, HC-SR04_Sensor_1.ECHO
  5V: Компонент1.5V, HC-SR04_Sensor_1.VCC, R1.pin_0
  N3: Компонент1.A0, R1.pin_1, R2.Pin_0
  N4: 7_Segment1.Segment_G, 7_Segment1.Segment_F
  N5: 7_Segment1.Segment_B, 7_Segment1.Segment_A
